# Fritzing sketch ddr (saved by Fritzing 0.9.3b)
stripboards: 1

parts:
  Part1 = Arduino Leonardo (Rev3b)
  S6 = Toggle Switch [part_number=blueRight package=THT]
  R1 = Resistor [tolerance=±5% resistance=10k package=THT]
  S7 = Toggle Switch [part_number=UP package=THT]
  S8 = Toggle Switch [part_number=RIGHT package=THT]
  S9 = Toggle Switch [part_number=DOWN package=THT]
  S10 = Toggle Switch [part_number=LEFT package=THT]
  S11 = Toggle Switch [part_number=blueRight package=THT]
  R2 = Resistor [tolerance=±5% resistance=10k package=THT]
  S12 = Toggle Switch [part_number=blueRight package=THT]
  R3 = Resistor [tolerance=±5% resistance=10k package=THT]
  J1 = double row male pin header, 6 pins [form="♂ (male)"]
  J2 = double row female pin header, 6 pins [form="♀ (female)"]

nets:
  N1: Part1.D0/RX, J2.pin4
  N2: Part1.D1/TX, J2.pin3
  N3: Part1.D2/SDA, J2.pin2
  N4: Part1.D3_PWM/SCL, J2.pin1
  N5: Part1.5V, R1.Pin_0, R2.Pin_0, R3.Pin_0, J2.pin5
  N6: Part1.GND, S6.COM, S11.COM, S12.COM
  N7: Part1.D8/A8, S6.L2, R1.Pin_1
  N8: Part1.D9_PWM/A9, S11.L2, R2.Pin_1
  N9: Part1.D10_PWM/A10, S12.L2, R3.Pin_1
  N10: S7.L1, S8.L1, S9.L1, S10.L1
  N11: S7.COM, J1.pin1
  N12: S7.L2, S8.L2, S9.L2, S10.L2
  N13: S8.COM, J1.pin2
  N14: S9.COM, J1.pin3
  N15: S10.COM, J1.pin4
